# Fritzing sketch proyectoV0 (saved by Fritzing 0.9.3b)
breadboards: 1

parts:
  Componente4 = Arduino Uno (Rev3) - ICSP
  Capacitive_Sol_Moisture_Sensor_V1_2 = Capacitive Sol Moisture Sensor V1.0
  Componente5 = Adafruit BMP180
  DHT2 = DHT11 Humitidy and Temperature Sensor
  Grove_Light_Sensor2 = Grove Light Sensor
  R2 = Resistor [tolerance=±5% resistance=10k package=THT]
  Board2 = LORABoard

nets:
  N1: Componente4.A0, Grove_Light_Sensor2.SIG
  N2: Componente4.A1, Capacitive_Sol_Moisture_Sensor_V1_2.A
  N3: Componente4.A4/SDA, Componente5.SDA
  N4: Componente4.A5/SCL, Componente5.SCL
  N5: Componente4.D10_PWM/SS, Board2.3
  N6: Componente4.D11_PWM/MOSI, Board2.4
  GND: Componente4.GND, Capacitive_Sol_Moisture_Sensor_V1_2.GND, Componente5.GND, DHT2.GND, Grove_Light_Sensor2.GND, Board2.1
  N7: Componente4.D5_PWM, DHT2.DATA, R2.Pin_1
  N8: Componente4.3V3, Board2.2
  VCC: Componente4.5V, Capacitive_Sol_Moisture_Sensor_V1_2.VCC, Componente5.+5V, Componente5.+3V3, DHT2.VDD, Grove_Light_Sensor2.VCC, R2.Pin_0

custom parts:
  Capacitive Sol Moisture Sensor V1.0: Soild moisture sensor developed by DFROBOT. It is resistant to corrosion.
  Adafruit BMP180: This precision sensor from Bosch is the best low-cost sensing solution for measuring barometric pressure and temperature. Because pressure changes with altitude you can also use it as an altimeter! The sensor is soldered onto a PCB with a 3.3V regulator, I2C level shifter and pull-up resistors on the I2C pins. The BMP180 is the next-generation of sensors from Bosch, and replaces the BMP085.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
  DHT11 Humitidy and Temperature Sensor: DHT11 Humidity and Temperature Sensor
  Grove Light Sensor: Light Sensor, Grove connector.
  LORABoard: LORA SX1272 RF Board by Libelium
